# Fritzing sketch TRZ (saved by Fritzing 0.9.9b)

parts:
  Componente1 = Arduino Nano (Rev3.0)
  Componente2 = BluePill
  Componente3 = InvenSense MPU6050
  Componente4 = Adafruit TCA9548A
  Componente5 = GY-VL53L0XV2 Laser Ranger Module
  Componente6 = GY-VL53L0XV2 Laser Ranger Module
  Componente7 = GY-VL53L0XV2 Laser Ranger Module
  Componente8 = GY-VL53L0XV2 Laser Ranger Module
  Componente9 = GY-VL53L0XV2 Laser Ranger Module
  Componente10 = GY-VL53L0XV2 Laser Ranger Module
  Componente11 = GY-VL53L0XV2 Laser Ranger Module
  Componente12 = GY-VL53L0XV2 Laser Ranger Module
  S1 = H-Bridge with L298N
  S2 = H-Bridge with L298N
  Mod1 = Raspberry Pi 4B  # not connected
  e-radionica1 = TCS230 Color Sensor [part_number=101209]
  M1 = DC Motor
  M2 = DC Motor
  M3 = DC Motor
  M4 = DC Motor
  J1 = Basic Servo
  USBTTL1 = USB A Plug
  USBTTL2 = Micro USB B Plug
  USBTTL3 = Micro USB B Plug
  USBTTL4 = USB A Plug
  USBTTL5 = USB A Plug
  USBTTL6 = Micro USB B Plug
  Mod2 = YL-99 Limit switch and LED
  Mod3 = YL-99 Limit switch and LED
  Mod4 = YL-99 Limit switch and LED
  Mod5 = YL-99 Limit switch and LED
  LED1 = smd LED [color="Red (633nm)" package="1206 [SMD]"]
  S3 = Round Pushbutton  # not connected

nets:
  N1: Componente1.A5, Componente3.SCL
  N2: Componente1.A4, Componente3.SDA, Componente3.XDA
  N3: Componente2.A0, e-radionica1.S0
  N4: Componente2.A5, e-radionica1.S1
  N5: Componente2.A6, e-radionica1.Out
  N6: Componente2.A7, e-radionica1.S2
  N7: Componente2.B0, e-radionica1.S3
  N8: Componente2.B9, Mod3.OUT
  N9: Componente2.B8, Mod5.OUT
  N10: Componente2.B7, Componente4.INPUTSDA
  N11: Componente2.B6, Componente4.INPUTSCL
  N12: Componente2.B5, LED1.anode
  N13: Componente2.B4, Mod2.OUT
  N14: Componente2.B3, S2.IN1, S2.IN3
  N15: Componente2.A10, S2.IN2, S2.IN4
  N16: Componente2.A9, S1.IN1, S1.IN3
  N17: Componente2.A8, S1.IN2, S1.IN4
  N18: Componente2.B1, J1.vcc, J1.pulse
  N19: Componente2.A2, Mod4.OUT
  N20: Componente4.2SDA, Componente7.SDA
  N21: Componente4.2SCL, Componente7.SCL
  N22: Componente4.3SDA, Componente6.SDA
  N23: Componente4.3SCL, Componente6.SCL
  N24: Componente4.4SDA, Componente5.SDA
  N25: Componente4.4SCL, Componente5.SCL
  N26: Componente4.5SDA, Componente12.SDA
  N27: Componente4.5SCL, Componente12.SCL
  N28: Componente4.6SDA, Componente11.SDA
  N29: Componente4.6SCL, Componente11.SCL
  N30: Componente4.7SDA, Componente10.SDA, Componente10.GPIO1
  N31: Componente4.7SCL, Componente10.SCL
  N32: Componente4.0SDA, Componente9.SDA
  N33: Componente4.0SCL, Componente9.SCL
  N34: Componente4.1SDA, Componente8.SDA
  N35: Componente4.1SCL, Componente8.SCL
  N36: S1.M1-01, M3.pin_2
  N37: S1.M1-02, M3.pin_1
  N38: S1.M2-01, M2.pin_1
  N39: S1.M2-02, M2.pin_2
  N40: S2.M1-01, M4.pin_2
  N41: S2.M1-02, M4.pin_1
  N42: S2.M2-01, M1.pin_1
  N43: S2.M2-02, M1.pin_2
  N44: USBTTL1.usb, USBTTL2.usb
  N45: USBTTL3.usb, USBTTL4.usb
  N46: USBTTL5.usb, USBTTL6.usb

custom parts:
  Adafruit TCA9548A: You just found the perfect I2C sensor, and you want to wire up two or three or more of them to your Arduino when you realize "Uh oh, this chip has a fixed I2C address, and from what I know about I2C, you cannot have two devices with the same address on the same SDA/SCL pins!" Are you out of luck? You would be, if you didn't have this ultra-cool TCA9548A 1-to-8 I2C multiplexer! Finally, a way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
  GY-VL53L0XV2 Laser Ranger Module: The GY-VL53L0XV2 is based on the VL53L0X from ST Microelectronics, a time-of-flight ranging system integrated into a compact module.
  H-Bridge with L298N: h-bridge
  TCS230 Color Sensor: TCS230
