# Fritzing sketch Schema Elettrico (saved by Fritzing 0.9.9b)

parts:
  Componente1 = BluePill
  Mod1 = Raspberry Pi 4B
  J1 = Basic Servo
  Componente3 = Adafruit TCA9548A
  Componente4 = GY-VL53L0XV2 Laser Ranger Module
  Componente5 = GY-VL53L0XV2 Laser Ranger Module
  Componente6 = GY-VL53L0XV2 Laser Ranger Module
  Componente7 = GY-VL53L0XV2 Laser Ranger Module
  Componente8 = GY-VL53L0XV2 Laser Ranger Module
  S1 = H-Bridge with L298N
  U1 = TCRT5000 [package=THT]
  S3 = Square Pushbutton
  GY1 = MPU-6050 Board GY-521 [form="♀ (female)" package=THT]
  S4 = Square Pushbutton

nets:
  N1: Componente1.A0, U1.Pin_1
  N2: Componente1.A1, J1.pulse
  N3: Componente1.A3, Mod1.GPIO14
  N4: Componente1.B10, Componente3.INPUTSCL
  N5: Componente1.B11, Componente3.INPUTSDA
  N6: Componente1.B7, GY1.pin4
  N7: Componente1.B6, GY1.pin3
  N8: Componente1.A12, S1.IN3
  N9: Componente1.A11, S1.IN4
  N10: Componente1.A10, S1.IN1
  N11: Componente1.A9, S1.IN2
  N12: Componente1.A8, U1.Pin_2
  N13: Componente1.A2, Mod1.GPIO15
  N14: Mod1.GND, Mod1.GPIO23, S3.leg0
  N15: Mod1.GPIO17, S4.leg1
  N16: Mod1.GPIO27, S4.leg0
  N17: Mod1.GPIO24, S3.leg1
  N18: Componente3.2SDA, Componente4.SDA
  N19: Componente3.2SCL, Componente5.SCL
  N20: Componente3.3SDA, Componente5.SDA
  N21: Componente3.3SCL, Componente4.SCL
  N22: Componente3.4SDA, Componente8.SDA
  N23: Componente3.4SCL, Componente8.SCL
  N24: Componente3.A2, Componente3.0SDA, Componente6.SDA
  N25: Componente3.0SCL, Componente6.SCL
  N26: Componente3.1SDA, Componente7.SDA
  N27: Componente3.1SCL, Componente7.SCL
  N28: S1.ENA, S1.ENB

notes:
  SCL/TX = Purple
  SDA/RX = Yellow
  5V = Red
  GND = Black
  PWM = Cyan
  C.Internal = Grey
  Analogic = Green

custom parts:
  Adafruit TCA9548A: You just found the perfect I2C sensor, and you want to wire up two or three or more of them to your Arduino when you realize "Uh oh, this chip has a fixed I2C address, and from what I know about I2C, you cannot have two devices with the same address on the same SDA/SCL pins!" Are you out of luck? You would be, if you didn't have this ultra-cool TCA9548A 1-to-8 I2C multiplexer! Finally, a way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
  GY-VL53L0XV2 Laser Ranger Module: The GY-VL53L0XV2 is based on the VL53L0X from ST Microelectronics, a time-of-flight ranging system integrated into a compact module.
  H-Bridge with L298N: h-bridge
  TCRT5000: TCRT5000 optical reflective sensor
  MPU-6050 Board GY-521: Acelerometro y Giroscopio MPU-6050 Board GY-521
